# Fritzing sketch AdafruitM0featherBLE_HealthThermometer (saved by Fritzing 0.9.3b)
breadboards: 1

parts:
  M0_Feather_Bluefruit_BLE = Adafruit Feather M0 Bluefruit LE [part_number="Adafruit #2995"]
  Grove_Infrared_Temperature_Sensor = Grove - Infrared Temperature Sensor
  Grove_Button = Grove Button
  Q1 = NPN-Transistor [package="TO92 [THT]"]
  R1 = Resistor [tolerance=±5% resistance=1k package=THT]
  Buzzer = Piezo Speaker
  Buckled_Cable1 = Grove Buckled Cable 5cm
  Buckled_Cable2 = Grove Buckled Cable 5cm

nets:
  N1: M0_Feather_Bluefruit_BLE.A3, R1.Pin_0
  N2: M0_Feather_Bluefruit_BLE.A1, Grove_Infrared_Temperature_Sensor.OBJ, Buckled_Cable1.NC
  N3: M0_Feather_Bluefruit_BLE.A0, Grove_Infrared_Temperature_Sensor.SUR, Buckled_Cable1.SIG
  GND: M0_Feather_Bluefruit_BLE.GND, Grove_Infrared_Temperature_Sensor.GND, Grove_Button.GND, Q1.E, Buckled_Cable1.GND, Buckled_Cable2.GND
  VCC: M0_Feather_Bluefruit_BLE.+3V3, Grove_Infrared_Temperature_Sensor.VCC, Grove_Button.VCC, Buzzer.pin2, Buckled_Cable1.VCC, Buckled_Cable2.VCC
  N4: M0_Feather_Bluefruit_BLE.D12, Grove_Button.SIG, Buckled_Cable2.SIG
  N5: Q1.B, R1.Pin_1
  N6: Q1.C, Buzzer.pin1

custom parts:
  Adafruit Feather M0 Bluefruit LE: This is the Adafruit Feather M0 Bluefruit LE - our take on an 'all-in-one' Arduino-compatible + Bluetooth Low Energy with built in USB and battery charging. Its an Adafruit Feather M0 with a BTLE module, ready to rock! We have other boards in the Feather family, check'em out here. Bluetooth Low Energy is the hottest new low-power, 2.4GHz spectrum wireless protocol. In particular, its the only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
  Grove - Infrared Temperature Sensor: This Grove-Infrared temperature sensor is a non-contact temperature measure model.The sensor is composed of 116 elements of thermocouple in series on a floating micro-membrane having an active diameter of 545μm and with blacken surface to absorb the incident thermal infrared radiation, which induces a voltage response at output terminals.
  Grove Buckled Cable 5cm: Grove - Universal 4 Pin Buckled 5cm Cable
